// Digital circuit 01.dig as structural Verilog
module _01 (
  input  [8:0] N,
  input  reset,
  input  start,
  input  clock,
  output done,
  output [7:0] displayout,
  output [15:0] clockcount,
  output valid,
  output [8:0] i,
  output [7:0] Data0,
  output fn0,
  output [8:0] j,
  output [7:0] Data_i,
  output [3:0] read_i
);

  wire add_1_c_o, add_2_c_o, and_2_out, and_3_out, and_4_out, and_5_out, and_6_out, comparator_1_eq,
       comparator_2_lt, comparator_3_eq, comparator_4_eq, d_ff_1_nq, finishRead, i__eq__eq__n_eq,
       i__lt__n_lt, j__lt__cnt_lt, n___eq__0_eq, or_2_out, or_3_out, read0, round;
  wire [7:0] multiplexer_2_out, ROMFILE_d;
  wire [8:0] add_1_s, add_2_s, cnt_2_out, cnt_out, multiplexer_1_out, multiplexer_3_out, multiplexer_5_out,
       multiplexer_6_out;

  or or_1 (finishRead, fn0, 1'b0, 1'b0, 1'b0, 1'b0, 1'b0, 1'b0, 1'b0, 1'b0, 1'b0, 1'b0, 1'b0, 1'b0, 1'b0, 1'b0, 1'b0);
  Counter #(.Bits(4)) counter_1 (.en(finishRead), .C(clock), .clr(1'b0), .out(read_i));  // open: ovf
  Demultiplexer #(.Selector_Bits(4)) demultiplexer_1 (
    .sel(read_i), .in(round), .out_0(read0));  // open: out_1, out_2, out_3, out_4, out_5, out_6, out_7, out_8, out_9, out_10, out_11, out_12, out_13, out_14, out_15
  and and_1 (fn0, d_ff_1_nq, and_2_out);
  D_FF d_ff_1 (.D(and_2_out), .C(clock), .nQ(d_ff_1_nq));  // open: Q
  Add #(.Bits(9)) add_1 (.a(j), .b({9{1'b0}}), .c_i(1'b1), .s(add_1_s), .c_o(add_1_c_o));
  and and_2 (and_2_out, read0, comparator_1_eq);
  Multiplexer #(.Bits(9)) multiplexer_1 (.sel(or_2_out), .in_0(j), .in_1(add_1_s), .out(multiplexer_1_out));
  or or_2 (or_2_out, add_1_c_o, j__lt__cnt_lt);
  Comparator #(.Bits(9)) comparator_1 (.a(cnt_out), .b(j), .eq(comparator_1_eq));  // open: gt, lt
  Comparator #(.Bits(9)) comparator_2 (.a(i), .b(N), .lt(comparator_2_lt));  // open: gt, eq
  Comparator #(.Bits(4)) comparator_3 (.a(Data_i[3:0]), .b(4'b0000), .eq(comparator_3_eq));  // open: gt, lt
  Comparator #(.Bits(4)) comparator_4 (.a(Data_i[7:4]), .b(4'b0000), .eq(comparator_4_eq));  // open: gt, lt
  Multiplexer #(.Selector_Bits(4), .Bits(8)) multiplexer_2 (
    .sel(read_i), .in_0(Data0), .in_1({8{1'b0}}), .in_2({8{1'b0}}), .in_3({8{1'b0}}), .in_4({8{1'b0}}),
    .in_5({8{1'b0}}), .in_6({8{1'b0}}), .in_7({8{1'b0}}), .in_8({8{1'b0}}), .in_9({8{1'b0}}),
    .in_10({8{1'b0}}), .in_11({8{1'b0}}), .in_12({8{1'b0}}), .in_13({8{1'b0}}), .in_14({8{1'b0}}),
    .in_15({8{1'b0}}), .out(multiplexer_2_out));
  Multiplexer #(.Bits(9)) multiplexer_3 (
    .sel(read0), .in_0({9{1'b0}}), .in_1(multiplexer_1_out), .out(multiplexer_3_out));
  and and_3 (and_3_out, comparator_2_lt, ~round, comparator_3_eq);  // And
  ROM #(.AddrBits(9), .isProgramMemory("true"), .Bits(8)) ROMFILE (.A(i), .sel(1'b1), .D(ROMFILE_d));
  D_FF #(.Bits(9)) u_j (.D(multiplexer_3_out), .C(clock), .Q(j));  // open: nQ
  Comparator #(.Bits(9)) j__lt__cnt (.a(j), .b(cnt_out), .lt(j__lt__cnt_lt));  // open: gt, eq
  and and_4 (and_4_out, comparator_4_eq, ~finishRead, round);  // And
  Comparator #(.Bits(9)) i__eq__eq__n (.a(i), .b(N), .eq(i__eq__eq__n_eq));  // open: gt, lt
  Counter #(.Bits(9)) cnt (.en(and_3_out), .C(clock), .clr(and_2_out), .out(cnt_out));  // open: ovf
  Multiplexer #(.Bits(8)) multiplexer_4 (.sel(round), .in_0(ROMFILE_d), .in_1(multiplexer_2_out), .out(Data_i));
  and and_5 (and_5_out, i__eq__eq__n_eq, start);
  Multiplexer #(.Bits(9)) multiplexer_5 (.sel(read0), .in_0(cnt_out), .in_1(j), .out(multiplexer_5_out));
  Counter #(.Bits(9)) cnt_2 (.en(and_4_out), .C(clock), .clr(1'b0), .out(cnt_2_out));  // open: ovf
  RAMDualPort #(.AddrBits(9), .Bits(8)) _0000_r0 (
    .A(multiplexer_5_out), .Din(Data_i), .str(and_3_out), .C(clock), .ld(read0), .D(Data0));
  RAMDualPort #(.AddrBits(9), .Bits(8)) _0000_r1 (
    .A(cnt_2_out), .Din(Data_i), .str(and_4_out), .C(clock), .ld(1'b0));  // open: D
  JK_FF u_Round (.J(and_5_out), .C(clock), .K(1'b0), .Q(round));  // open: nQ
  Comparator #(.Bits(9)) n___eq__0 (.a(N), .b({9{1'b0}}), .eq(n___eq__0_eq));  // open: gt, lt
  and and_6 (and_6_out, ~n___eq__0_eq, start);  // And
  D_FF_AS #(.Bits(9)) i__0_n (.Set(~and_6_out), .D(multiplexer_6_out), .C(clock), .Clr(reset), .Q(i));  // open: nQ
  Add #(.Bits(9)) add_2 (.a(i), .b({9{1'b0}}), .c_i(1'b1), .s(add_2_s), .c_o(add_2_c_o));
  Multiplexer #(.Bits(9)) multiplexer_6 (.sel(or_3_out), .in_0(i), .in_1(add_2_s), .out(multiplexer_6_out));
  or or_3 (or_3_out, add_2_c_o, i__lt__n_lt);
  Comparator #(.Bits(9)) i__lt__n (.a(i), .b(N), .lt(i__lt__n_lt));  // open: gt, eq
  Seven_Seg_Hex seven_seg_hex_1 (.d(4'b0000), .dp(1'b0));
  Seven_Seg_Hex seven_seg_hex_2 (.d(4'b0000), .dp(1'b0));

  assign clockcount = {16{1'b0}};
  assign displayout = {8{1'b0}};
  assign done = 1'b0;
  assign valid = 1'b0;

  // Other names for the same wires on the sheet: Clk = clock; finishRead0 = fn0

  // Notes on the sheet:
  //   contents of ROMFILE (hex, n*v repeats v):
  //   10,1adb0,208,0,e,50,f,2710
endmodule
