// Digital circuit BBBLab10.dig as structural Verilog
module BBBLab10 (
  input  start,
  input  [8:0] N,
  input  reset,
  input  clock,
  output [7:0] displayout,
  output valid,
  output done,
  output [15:0] clockcount
);

  wire and_1_out, and_2_out, and_3_out, and_4_out, and_5_out, and_6_out, and_7_out, and_8_out, and_9_out,
       and_10_out, and_11_out, and_12_out, comparator_1_lt, comparator_2_lt, comparator_3_lt,
       comparator_4_lt, comparator_5_eq, comparator_7_lt, comparator_8_eq, done_t, newR, not_1_out,
       not_2_out, P2, P3;
  wire [7:0] counter_4_out, multiplexer_1_out, ROMFILE_d;
  wire [8:0] A, A_plus_1, add_2_s, add_3_s, counter_1_out, counter_6_out, multiplexer_2_out, print, round;

  Add #(.Bits(9)) add_1 (.a(A), .b(9'h1), .c_i(1'b0), .s(A_plus_1));  // open: c_o
  Comparator #(.Bits(9)) comparator_1 (.a(counter_1_out), .b(N), .eq(P2), .lt(comparator_1_lt));  // open: gt
  and and_1 (and_1_out, start, comparator_1_lt);
  Counter #(.Bits(9)) counter_1 (.en(and_1_out), .C(clock), .clr(reset), .out(counter_1_out));  // open: ovf
  and and_2 (and_2_out, P2, start);
  and and_3 (and_3_out, clock, ~P2, start);  // And
  and and_4 (and_4_out, P2, start);
  and and_5 (and_5_out, P3, start);
  ROM #(.AddrBits(9), .isProgramMemory("true"), .Bits(8)) ROMFILE (.A(counter_1_out), .sel(start), .D(ROMFILE_d));
  Comparator #(.Bits(9)) comparator_2 (.a(A), .b(N), .lt(comparator_2_lt));  // open: gt, eq
  Comparator #(.Bits(8)) comparator_3 (.a(counter_4_out), .b({8{1'b1}}), .lt(comparator_3_lt));  // open: gt, eq
  Comparator #(.Bits(9)) comparator_4 (.a(print), .b(N), .eq(done_t), .lt(comparator_4_lt));  // open: gt
  and and_6 (and_6_out, comparator_2_lt, and_2_out);
  and and_7 (and_7_out, comparator_4_lt, and_5_out);
  Comparator #(.Bits(9)) comparator_5 (.a(round), .b({9{1'b0}}), .eq(comparator_5_eq));  // open: gt, lt
  not not_1 (not_1_out, comparator_5_eq);
  and and_8 (and_8_out, newR, ~done_t, comparator_3_lt, and_4_out);  // And
  Counter #(.Bits(9)) counter_2 (.en(and_7_out), .C(clock), .clr(reset), .out(print));  // open: ovf
  and and_9 (and_9_out, not_1_out, and_6_out);
  Comparator #(.Bits(9)) comparator_6 (.a(A), .b(N), .eq(P3));  // open: gt, lt
  Counter #(.Bits(9)) counter_3 (.en(and_9_out), .C(clock), .clr(reset), .out(A));  // open: ovf
  Counter #(.Bits(8)) counter_4 (.en(and_8_out), .C(clock), .clr(reset), .out(counter_4_out));  // open: ovf
  Multiplexer #(.Bits(8)) multiplexer_1 (.sel(P2), .in_0(ROMFILE_d), .in_1(counter_4_out), .out(multiplexer_1_out));
  Multiplexer #(.Bits(9)) multiplexer_2 (.sel(P3), .in_0(A), .in_1(print), .out(multiplexer_2_out));
  RAMDualPort #(.AddrBits(8), .Bits(9)) ramdualport_1 (
    .A(multiplexer_1_out), .Din(add_2_s), .str(and_3_out), .C(and_3_out), .ld(1'b1), .D(round));
  and and_10 (and_10_out, start, ~done_t);  // And
  Add #(.Bits(9)) add_2 (.a(round), .b({9{1'b0}}), .c_i(1'b1), .s(add_2_s));  // open: c_o
  Comparator #(.Bits(9)) comparator_7 (.a(add_3_s), .b(round), .lt(comparator_7_lt));  // open: gt, eq
  Add #(.Bits(9)) add_3 (.a(counter_6_out), .b(9'h1), .c_i(1'b0), .s(add_3_s));  // open: c_o
  Counter #(.Bits(16)) counter_5 (.en(and_10_out), .C(clock), .clr(1'b0), .out(clockcount));  // open: ovf
  RAMDualPort #(.AddrBits(9), .Bits(8)) RAM (
    .A(multiplexer_2_out), .Din(counter_4_out), .str(and_9_out), .C(clock), .ld(1'b1), .D(displayout));
  Comparator #(.Bits(9)) comparator_8 (.a(round), .b({9{1'b0}}), .eq(comparator_8_eq));  // open: gt, lt
  and and_11 (and_11_out, P2, comparator_7_lt);
  not not_2 (not_2_out, comparator_7_lt);
  or or_1 (newR, not_2_out, comparator_8_eq);
  Counter #(.Bits(9)) counter_6 (.en(and_11_out), .C(clock), .clr(newR), .out(counter_6_out));  // open: ovf
  Seven_Seg_Hex seven_seg_hex_1 (.d(displayout[7:4]), .dp(1'b0));
  and and_12 (and_12_out, P3, start);
  Seven_Seg_Hex seven_seg_hex_2 (.d(displayout[3:0]), .dp(1'b0));
  and and_13 (valid, and_12_out, ~done_t);  // And
  and and_14 (done, P3, done_t);

  // Notes on the sheet:
  //   N: default 511
  //   contents of ROMFILE (hex, n*v repeats v):
  //   1,5,4,9,6,3,7,8,2
endmodule

/* Test case FINALT0:
clock N reset start valid displayout done clockcount
            program(4,3,1,2)
0 4 0 0 X X X X
1 4 0 0 X X X X
0 4 1 0 X X X X
1 4 1 0 X X X X
0 4 0 1 X X X X
1 4 0 1 X X X X
repeat (40000) C 4 0 1 X X X X
1 4 0 1 X X X 0xBAADBEEF
*/

/* Test case FINALT1:
clock N reset start valid displayout done clockcount
            program(255,2,3,2)
0 4 0 0 X X X X
1 4 0 0 X X X X
0 4 1 0 X X X X
1 4 1 0 X X X X
0 4 0 1 X X X X
1 4 0 1 X X X X
repeat (40000) C 4 0 1 X X X X
1 4 0 1 X X X 0xBAADBEEF
*/

/* Test case FINALT2:
clock N reset start valid displayout done clockcount
            program(0,1,2,3,4,5,6,7,8,9,10,11,12,13,14,15,16,17,18,19,20,21,22,23,24,25,26,27,28,29,30,31,32,33,34,35,36,37,38,39,40,41,42,43,44,45,46,47,48,49,50,51,52,53,54,55,56,57,58,59,60,61,62,63,64,65,66,67,68,69,70,71,72,73,74,75,76,77,78,79,80,81,82,83,84,85,86,87,88,89,90,91,92,93,94,95,96,97,98,99,100,101,102,103,104,105,106,107,108,109,110,111,112,113,114,115,116,117,118,119,120,121,122,123,124,125,126,127,128,129,130,131,132,133,134,135,136,137,138,139,140,141,142,143,144,145,146,147,148,149,150,151,152,153,154,155,156,157,158,159,160,161,162,163,164,165,166,167,168,169,170,171,172,173,174,175,176,177,178,179,180,181,182,183,184,185,186,187,188,189,190,191,192,193,194,195,196,197,198,199,200,201,202,203,204,205,206,207,208,209,210,211,212,213,214,215,216,217,218,219,220,221,222,223,224,225,226,227,228,229,230,231,232,233,234,235,236,237,238,239,240,241,242,243,244,245,246,247,248,249,250,251,252,253,254,255)
0 256 0 0 X X X X
1 256 0 0 X X X X
0 256 1 0 X X X X
1 256 1 0 X X X X
0 256 0 1 X X X X
1 256 0 1 X X X X
repeat (40000) C 256 0 1 X X X X
1 256 0 1 X X X 0xBAADBEEF
*/

/* Test case FINALT3:
clock N reset start valid displayout done clockcount
            program(0,0,1,1,2,2,3,3,4,4,5,5,6,6,7,7,8,8,9,9,10,10,11,11,12,12,13,13,14,14,15,15,16,16,17,17,18,18,19,19,20,20,21,21,22,22,23,23,24,24,25,25,26,26,27,27,28,28,29,29,30,30,31,31,32,32,33,33,34,34,35,35,36,36,37,37,38,38,39,39,40,40,41,41,42,42,43,43,44,44,45,45,46,46,47,47,48,48,49,49,50,50,51,51,52,52,53,53,54,54,55,55,56,56,57,57,58,58,59,59,60,60,61,61,62,62,63,63,64,64,65,65,66,66,67,67,68,68,69,69,70,70,71,71,72,72,73,73,74,74,75,75,76,76,77,77,78,78,79,79,80,80,81,81,82,82,83,83,84,84,85,85,86,86,87,87,88,88,89,89,90,90,91,91,92,92,93,93,94,94,95,95,96,96,97,97,98,98,99,99,100,100,101,101,102,102,103,103,104,104,105,105,106,106,107,107,108,108,109,109,110,110,111,111,112,112,113,113,114,114,115,115,116,116,117,117,118,118,119,119,120,120,121,121,122,122,123,123,124,124,125,125,126,126,127,127,128,128,129,129,130,130,131,131,132,132,133,133,134,134,135,135,136,136,137,137,138,138,139,139,140,140,141,141,142,142,143,143,144,144,145,145,146,146,147,147,148,148,149,149,150,150,151,151,152,152,153,153,154,154,155,155,156,156,157,157,158,158,159,159,160,160,161,161,162,162,163,163,164,164,165,165,166,166,167,167,168,168,169,169,170,170,171,171,172,172,173,173,174,174,175,175,176,176,177,177,178,178,179,179,180,180,181,181,182,182,183,183,184,184,185,185,186,186,187,187,188,188,189,189,190,190,191,191,192,192,193,193,194,194,195,195,196,196,197,197,198,198,199,199,200,200,201,201,202,202,203,203,204,204,205,205,206,206,207,207,208,208,209,209,210,210,211,211,212,212,213,213,214,214,215,215,216,216,217,217,218,218,219,219,220,220,221,221,222,222,223,223,224,224,225,225,226,226,227,227,228,228,229,229,230,230,231,231,232,232,233,233,234,234,235,235,236,236,237,237,238,238,239,239,240,240,241,241,242,242,243,243,244,244,245,245,246,246,247,247,248,248,249,249,250,250,251,251,252,252,253,253,254,254)
0 510 0 0 X X X X
1 510 0 0 X X X X
0 510 1 0 X X X X
1 510 1 0 X X X X
0 510 0 1 X X X X
1 510 0 1 X X X X
repeat (40000) C 510 0 1 X X X X
1 510 0 1 X X X 0xBAADBEEF
*/

/* Test case FINALT4:
clock N reset start valid displayout done clockcount
            program(99,183,239,24,109,113,147,248,108,168,224,36,130,98,82,45,227,187,98,241,166,122,206,216,106,32,220,239,155,108,56,168,136,202,194,117,216,39,207,214,3,237,110,48,176,11,189,184,4,134,78,17,221,92,142,33,77,207,185,243,85,255,159)
0 63 0 0 X X X X
1 63 0 0 X X X X
0 63 1 0 X X X X
1 63 1 0 X X X X
0 63 0 1 X X X X
1 63 0 1 X X X X
repeat (40000) C 63 0 1 X X X X
1 63 0 1 X X X 0xBAADBEEF
*/

/* Test case FINALT5:
clock N reset start valid displayout done clockcount
            program(255,254,253,252,251,250,249,248,247,246,245,244,243,242,241,240,239,238,237,236,235,234,233,232,231,230,229,228,227,226,225,224,223,222,221,220,219,218,217,216,215,214,213,212,211,210,209,208,207,206,205,204,203,202,201,200,199,198,197,196,195,194,193)
0 63 0 0 X X X X
1 63 0 0 X X X X
0 63 1 0 X X X X
1 63 1 0 X X X X
0 63 0 1 X X X X
1 63 0 1 X X X X
repeat (40000) C 63 0 1 X X X X
1 63 0 1 X X X 0xBAADBEEF
*/

/* Test case FINALT6:
clock N reset start valid displayout done clockcount
            program(92,3,43,33,16,177,226,60,235,71,91,102,228,71,41,76,159,172,192,34,30,179,237,29,98,142,167,46,143,78,128,238,104,217,57,163,125,48,143,90,6,7,202,234,22,172,122,139,241,100,161,171,9,68,147,176,186,206,205,27,112,33,110,75,61,74,175,62,189,12,229,103,186,106,65,234,162,153,154,130,123,222,104,232,152,20,125,25,175,224,224,26,137,104,17,238,29,6,210,231,140,73,249,31,18,136,62,44,230,173,37,75,240,213,55,135,3,122,182,110,49,118,98,80,88,98,229)
0 127 0 0 X X X X
1 127 0 0 X X X X
0 127 1 0 X X X X
1 127 1 0 X X X X
0 127 0 1 X X X X
1 127 0 1 X X X X
repeat (40000) C 127 0 1 X X X X
1 127 0 1 X X X 0xBAADBEEF
*/

/* Test case FINALT7:
clock N reset start valid displayout done clockcount
            program(255,254,253,252,251,250,249,248,247,246,245,244,243,242,241,240,239,238,237,236,235,234,233,232,231,230,229,228,227,226,225,224,223,222,221,220,219,218,217,216,215,214,213,212,211,210,209,208,207,206,205,204,203,202,201,200,199,198,197,196,195,194,193,192,191,190,189,188,187,186,185,184,183,182,181,180,179,178,177,176,175,174,173,172,171,170,169,168,167,166,165,164,163,162,161,160,159,158,157,156,155,154,153,152,151,150,149,148,147,146,145,144,143,142,141,140,139,138,137,136,135,134,133,132,131,130,129)
0 127 0 0 X X X X
1 127 0 0 X X X X
0 127 1 0 X X X X
1 127 1 0 X X X X
0 127 0 1 X X X X
1 127 0 1 X X X X
repeat (40000) C 127 0 1 X X X X
1 127 0 1 X X X 0xBAADBEEF
*/

/* Test case FINALT8:
clock N reset start valid displayout done clockcount
            program(70,19,96,116,53,6,170,65,246,65,56,56,20,229,46,140,206,68,30,59,147,31,49,152,147,120,84,198,194,77,170,16,122,156,199,123,240,124,102,208,77,84,253,224,249,99,140,13,97,168,19,114,159,135,17,192,65,130,189,234,135,28,232,154,46,90,10,190,246,22,196,22,181,29,118,1,194,64,250,200,53,95,215,224,138,188,109,145,203,70,84,249,152,118,215,23,27,54,5,250,146,233,190,147,69,186,245,124,69,226,32,198,51,246,49,31,232,139,177,195,84,39,119,213,214,88,27,191,52,6,87,130,81,64,147,126,44,98,71,26,96,243,61,75,246,255,156,94,71,95,81,255,217,246,30,87,183,38,128,91,2,3,164,19,79,136,117,81,209,125,101,164,75,171,179,196,163,115,154,150,146,216,80,74,5,193,55,223,92,128,108,228,252,107,64,53,41,212,202,5,155,89,65,207,31,181,41,90,104,157,0,88,27,197,186,102,247,77,118,185,88,6,253,238,120,158,225,164,35,215,224,181,19,178,249,20,37,187,177,167,35,29,41,239,193,153,114,140,111,89,103,69,146,137,52)
0 255 0 0 X X X X
1 255 0 0 X X X X
0 255 1 0 X X X X
1 255 1 0 X X X X
0 255 0 1 X X X X
1 255 0 1 X X X X
repeat (40000) C 255 0 1 X X X X
1 255 0 1 X X X 0xBAADBEEF
*/

/* Test case FINALT9:
clock N reset start valid displayout done clockcount
            program(255,254,253,252,251,250,249,248,247,246,245,244,243,242,241,240,239,238,237,236,235,234,233,232,231,230,229,228,227,226,225,224,223,222,221,220,219,218,217,216,215,214,213,212,211,210,209,208,207,206,205,204,203,202,201,200,199,198,197,196,195,194,193,192,191,190,189,188,187,186,185,184,183,182,181,180,179,178,177,176,175,174,173,172,171,170,169,168,167,166,165,164,163,162,161,160,159,158,157,156,155,154,153,152,151,150,149,148,147,146,145,144,143,142,141,140,139,138,137,136,135,134,133,132,131,130,129,128,127,126,125,124,123,122,121,120,119,118,117,116,115,114,113,112,111,110,109,108,107,106,105,104,103,102,101,100,99,98,97,96,95,94,93,92,91,90,89,88,87,86,85,84,83,82,81,80,79,78,77,76,75,74,73,72,71,70,69,68,67,66,65,64,63,62,61,60,59,58,57,56,55,54,53,52,51,50,49,48,47,46,45,44,43,42,41,40,39,38,37,36,35,34,33,32,31,30,29,28,27,26,25,24,23,22,21,20,19,18,17,16,15,14,13,12,11,10,9,8,7,6,5,4,3,2,1)
0 255 0 0 X X X X
1 255 0 0 X X X X
0 255 1 0 X X X X
1 255 1 0 X X X X
0 255 0 1 X X X X
1 255 0 1 X X X X
repeat (40000) C 255 0 1 X X X X
1 255 0 1 X X X 0xBAADBEEF
*/

/* Test case FINALT10:
clock N reset start valid displayout done clockcount
            program(73,182,14,93,212,160,144,191,172,74,212,115,222,31,12,157,189,100,120,169,87,38,158,41,157,139,77,177,9,113,123,17,3,147,204,42,235,175,50,205,195,198,171,212,35,55,132,157,240,37,214,101,78,10,115,250,81,56,43,82,144,96,194,237,38,82,145,171,80,44,102,142,20,93,178,28,207,16,86,215,22,104,66,99,247,43,199,77,216,90,194,169,40,50,14,209,76,235,80,130,233,62,93,54,230,93,102,114,28,3,66,158,104,170,121,247,42,62,24,109,127,253,229,57,184,33,124,162,150,91,26,227,92,140,38,5,19,61,34,37,71,202,145,27,31,65,56,254,223,139,57,250,168,78,175,225,121,164,75,93,227,217,128,18,116,100,19,93,228,245,167,148,57,235,143,181,141,129,215,125,211,174,105,173,9,92,163,118,52,208,252,91,171,128,121,18,10,187,111,216,55,128,91,236,4,143,71,202,146,33,54,147,68,2,92,254,40,126,8,185,135,135,252,34,115,251,237,210,76,100,141,209,174,90,210,249,58,125,187,193,238,48,13,140,221,245,162,189,250,91,164,67,62,157,77,214,243,129,156,60,22,242,31,119,191,166,115,233,130,137,164,231,191,237,29,187,192,78,216,145,187,85,201,253,163,247,206,40,59,3,36,49,114,246,113,166,101,30,3,113,29,124,140,253,129,130,224,37,184,17,69,23,252,74,34,211,245,206,69,23,105,87,59,81,157,101,151,214,119,89,34,210,113,254,76,245,233,188,163,152,85,143,176,139,249,133,101,247,98,213,27,210,36,228,41,4,188,228,171,206,114,143,13,146,116,8,174,103,108,252,113,35,148,181,244,96,82,89,66,24,186,23,180,167,185,63,49,73,185,65,112,95,211,221,5,56,246,8,145,180,194,217,230,104,233,228,50,48,88,228,184,21,95,166,53,228,198,141,53,23,15,47,69,208,202,33,116,40,60,178,125,212,50,54,171,175,212,92,40,123,18,9,93,220,5,126,147,147,181,55,117,53,206,198,6,180,133,126,71,100,45,231,7,197,56,131,114,199,44,241,171,178,230,135,203,149,176,247,31,224,42,222,73,122,1,161,150,134,115,178,98,194,57,161,167,3,179,216,117,167,164,9,155,158,238,70,61,163,200,201,151)
0 511 0 0 X X X X
1 511 0 0 X X X X
0 511 1 0 X X X X
1 511 1 0 X X X X
0 511 0 1 X X X X
1 511 0 1 X X X X
repeat (40000) C 511 0 1 X X X X
1 511 0 1 X X X 0xBAADBEEF
*/

/* Test case FINALT11:
clock N reset start valid displayout done clockcount
            program(1,1,1,1,1,1,1,1,1,1,1,1,1,1,1,1,1,1,1,1,1,1,1,1,1,1,1,1,1,1,1,1,1,1,1,1,1,1,1,1,1,1,1,1,1,1,1,1,1,1,1,1,1,1,1,1,1,1,1,1,1,1,1,1,1,1,1,1,1,1,1,1,1,1,1,1,1,1,1,1,1,1,1,1,1,1,1,1,1,1,1,1,1,1,1,1,1,1,1,1,1,1,1,1,1,1,1,1,1,1,1,1,1,1,1,1,1,1,1,1,1,1,1,1,1,1,1,1,1,1,1,1,1,1,1,1,1,1,1,1,1,1,1,1,1,1,1,1,1,1,1,1,1,1,1,1,1,1,1,1,1,1,1,1,1,1,1,1,1,1,1,1,1,1,1,1,1,1,1,1,1,1,1,1,1,1,1,1,1,1,1,1,1,1,1,1,1,1,1,1,1,1,1,1,1,1,1,1,1,1,1,1,1,1,1,1,1,1,1,1,1,1,1,1,1,1,1,1,1,1,1,1,1,1,1,1,1,1,1,1,1,1,1,1,1,1,1,1,1,1,1,1,1,1,1,1,1,1,1,1,1,1,1,1,1,1,1,1,1,1,1,1,1,1,1,1,1,1,1,1,1,1,1,1,1,1,1,1,1,1,1,1,1,1,1,1,1,1,1,1,1,1,1,1,1,1,1,1,1,1,1,1,1,1,1,1,1,1,1,1,1,1,1,1,1,1,1,1,1,1,1,1,1,1,1,1,1,1,1,1,1,1,1,1,1,1,1,1,1,1,1,1,1,1,1,1,1,1,1,1,1,1,1,1,1,1,1,1,1,1,1,1,1,1,1,1,1,1,1,1,1,1,1,1,1,1,1,1,1,1,1,1,1,1,1,1,1,1,1,1,1,1,1,1,1,1,1,1,1,1,1,1,1,1,1,1,1,1,1,1,1,1,1,1,1,1,1,1,1,1,1,1,1,1,1,1,1,1,1,1,1,1,1,1,1,1,1,1,1,1,1,1,1,1,1,1,1,1,1,1,1,1,1,1,1,1,1,1,1,1,1,1,1,1,1,1,1,1,1,1,1,1,1,1,1,1,1,1,1,1,1,1,1,1,1,1,1,1,1,1,1,1,1,1,1,1,1,1,1,1,1)
0 511 0 0 X X X X
1 511 0 0 X X X X
0 511 1 0 X X X X
1 511 1 0 X X X X
0 511 0 1 X X X X
1 511 0 1 X X X X
repeat (40000) C 511 0 1 X X X X
1 511 0 1 X X X 0xBAADBEEF
*/
