// Digital circuit sol.dig as structural Verilog
module sol (
  input  [8:0] N,
  input  reset,
  input  start,
  input  clock,
  output done,
  output [7:0] displayout,
  output [15:0] clockcount,
  output valid
);

  wire and_1_out, and_2_out, and_3_out, and_4_out, and_6_out, and_7_out, comparator_1_eq, comparator_1_gt,
       comparator_3_gt, comparator_4_eq, count__ok, goNext, jk_ff_2_nq, not_1_out, or_1_out, or_2_out;
  wire [7:0] multiplexer_1_out, ROMFILE_d;
  wire [8:0] add_1_s, add_2_s, cnt, counter_3_out, counter_4_out, RAM_d1, RAM_d2;

  and and_1 (and_1_out, start, ~count__ok);  // And
  and and_2 (and_2_out, goNext, ~done);  // And
  Counter #(.Bits(9)) counter_1 (.en(and_1_out), .C(clock), .clr(reset), .out(cnt));  // open: ovf
  ROM #(.AddrBits(9), .isProgramMemory("true"), .Bits(8)) ROMFILE (.A(cnt), .sel(and_1_out), .D(ROMFILE_d));
  Counter #(.Bits(8)) counter_2 (.en(and_2_out), .C(clock), .clr(reset), .out(displayout));  // open: ovf
  Add #(.Bits(9)) add_1 (.a(cnt), .b(9'h1), .c_i(1'b0), .s(add_1_s));  // open: c_o
  not not_1 (not_1_out, count__ok);
  and and_3 (and_3_out, not_1_out, start);
  Comparator #(.Bits(9)) comparator_1 (.a(add_1_s), .b(N), .gt(comparator_1_gt), .eq(comparator_1_eq));  // open: lt
  Multiplexer #(.Bits(8)) multiplexer_1 (.sel(count__ok), .in_0(ROMFILE_d), .in_1(displayout), .out(multiplexer_1_out));
  or or_1 (or_1_out, comparator_1_gt, comparator_1_eq);
  or or_2 (or_2_out, reset, goNext);
  and and_4 (and_4_out, or_1_out, ~reset, start);  // And
  RAMDualAccess #(.AddrBits(8), .Bits(9)) RAM (
    .str(and_3_out), .C(clock), .ld(count__ok), .A1(multiplexer_1_out), .Din1(add_2_s), .A2(ROMFILE_d),
    .D1(RAM_d1), .D2(RAM_d2));
  JK_FF jk_ff_1 (.J(and_4_out), .C(clock), .K(reset), .Q(count__ok));  // open: nQ
  Counter #(.Bits(9)) counter_3 (.en(count__ok), .C(clock), .clr(or_2_out), .out(counter_3_out));  // open: ovf
  Add #(.Bits(9)) add_2 (.a(RAM_d2), .b({9{1'b0}}), .c_i(1'b1), .s(add_2_s));  // open: c_o
  Comparator #(.Bits(9)) comparator_2 (.a(counter_3_out), .b(RAM_d1), .eq(goNext));  // open: gt, lt
  Comparator #(.Bits(9)) comparator_3 (.a(counter_3_out), .b({9{1'b0}}), .gt(comparator_3_gt));  // open: eq, lt
  Counter #(.Bits(9)) counter_4 (.en(valid), .C(clock), .clr(reset), .out(counter_4_out));  // open: ovf
  and and_5 (valid, comparator_3_gt, count__ok);
  Comparator #(.Bits(9)) comparator_4 (.a(counter_4_out), .b(N), .eq(comparator_4_eq));  // open: gt, lt
  and and_6 (and_6_out, jk_ff_2_nq, start);
  Seven_Seg_Hex seven_seg_hex_1 (.d(displayout[7:4]), .dp(1'b0));
  and and_7 (and_7_out, comparator_4_eq, ~reset, start);  // And
  Seven_Seg_Hex seven_seg_hex_2 (.d(displayout[3:0]), .dp(1'b0));
  Counter #(.Bits(16)) counter_5 (.en(and_6_out), .C(clock), .clr(reset), .out(clockcount));  // open: ovf
  JK_FF jk_ff_2 (.J(and_7_out), .C(clock), .K(reset), .Q(done), .nQ(jk_ff_2_nq));

  // Other names for the same wires on the sheet: display[7:0] = displayout

  // Notes on the sheet:
  //   N: default 4
  //   clock: Hz: 50
  //   contents of ROMFILE (hex, n*v repeats v):
  //   c2,2,3,2,1,7,4,2,1,2,3,4,5,c
endmodule
