// Digital circuit template.dig as structural Verilog
module template (
  input  [8:0] N,
  input  reset,
  input  start,
  input  clock,
  output done,
  output [7:0] displayout,
  output [15:0] clockcount,
  output valid
);

  wire add_1_s, Clk, finishRead0, multiplexer_2_out, or_1_out;
  wire [1:0] curPos;
  wire [7:0] multiplexer_1_out, undriven;

  Add add_1 (.a(curPos[0]), .b(1'b0), .c_i(1'b1), .s(add_1_s));  // open: c_o
  buf or_1 (or_1_out, finishRead0);  // Or open: In_2, In_3, In_4
  Multiplexer #(.Selector_Bits(2), .Bits(8)) multiplexer_1 (
    .sel(curPos), .in_0(undriven), .out(multiplexer_1_out));  // open: in_1, in_2, in_3
  Multiplexer multiplexer_2 (.sel(or_1_out), .in_0(curPos[0]), .in_1(add_1_s), .out(multiplexer_2_out));
  RAMDualPort Collector_0000_0011 (.Din(multiplexer_1_out[0]), .C(Clk));  // open: A, str, ld, D
  ROM #(.AddrBits(9), .Bits(8)) ROMFILE ();  // open: A, sel, D
  D_FF_AS d_ff_as_1 (.Set(1'b0), .D(multiplexer_2_out), .C(Clk), .Q(curPos[0]));  // open: Clr, nQ
  Seven_Seg_Hex seven_seg_hex_1 (.d(displayout[7:4]), .dp(1'b0));
  RAMDualPort #(.AddrBits(9), .Bits(8)) RAM ();  // open: A, Din, str, C, ld, D
  Seven_Seg_Hex seven_seg_hex_2 (.d(displayout[3:0]), .dp(1'b0));
  // Pins of 1 and 8 bits meet at multiplexer_1_out
  // Pins of 1 and 2 bits meet at curPos
endmodule
