// Digital circuit 01.dig as structural Verilog
module _01 (
  input  [3:0] In,
  input  [1:0] Selector,
  output [3:0] Output
);

  wire [3:0] _2_4_2_1_code_1_out, _6_4_2__3_code_1_out, cyclic_1_out, excess_3_1_out;

  Excess_3 excess_3_1 (.In(In), .Out(excess_3_1_out));
  Cyclic cyclic_1 (.In(In), .Out(cyclic_1_out));
  _2_4_2_1_Code _2_4_2_1_code_1 (.In(In), .Out(_2_4_2_1_code_1_out));
  _6_4_2__3_Code _6_4_2__3_code_1 (.In(In), .Out(_6_4_2__3_code_1_out));
  Multiplexer #(.Bits(4), .Selector_Bits(2)) multiplexer_1 (
    .sel(Selector), .in_0(excess_3_1_out), .in_1(cyclic_1_out), .in_2(_2_4_2_1_code_1_out),
    .in_3(_6_4_2__3_code_1_out), .out(Output));
endmodule
