// Digital circuit Template.dig as structural Verilog
module Template (
  input  [6:0] In,
  output [6:0] Output
);

  wire [2:0] get_c1c2c3_1_out;
  wire [6:0] transfrom_to_7bits_1_out;

  Get_C1C2C3 get_c1c2c3_1 (.In(In), .Out(get_c1c2c3_1_out));
  Transfrom_to_7bits transfrom_to_7bits_1 (.In(get_c1c2c3_1_out), .Out(transfrom_to_7bits_1_out));
  Invert_selected_bit invert_selected_bit_1 (.In(transfrom_to_7bits_1_out), .Corrector(In), .Out(Output));
endmodule
