// Digital circuit Transfrom to 7bits.dig as structural Verilog
module Transfrom_to_7bits (
  input  [2:0] In,
  output [6:0] Out
);

  wire not_1_out, not_2_out, not_3_out;

  not not_1 (not_1_out, In[2]);
  not not_2 (not_2_out, In[1]);
  not not_3 (not_3_out, In[0]);
  and and_1 (Out[6], not_1_out, not_2_out, In[0]);
  and and_2 (Out[5], not_1_out, In[1], not_3_out);
  and and_3 (Out[4], not_1_out, In[1], In[0]);
  and and_4 (Out[3], In[2], not_2_out, not_3_out);
  and and_5 (Out[2], In[2], not_2_out, In[0]);
  and and_6 (Out[1], In[2], In[1], not_3_out);
  and and_7 (Out[0], In[2], In[1], In[0]);
endmodule
