// Digital circuit Get C1C2C3.dig as structural Verilog
module Get_C1C2C3 (
  input  [6:0] In,
  output [2:0] Out
);

  xor xor_1 (Out[2], In[3], In[2], In[1], In[0]);
  xor xor_2 (Out[1], In[5], In[4], In[1], In[0]);
  xor xor_3 (Out[0], In[6], In[4], In[2], In[0]);
endmodule
