// Digital circuit Invert selected bit.dig as structural Verilog
module Invert_selected_bit (
  input  [6:0] In,
  input  [6:0] Corrector,
  output [6:0] Out
);

  assign Out = In ^ Corrector;  // XOr xor_1, 7 bits wide
endmodule
