// Digital circuit 03.dig as structural Verilog
module _03 (
  input  [7:0] In,
  output [8:0] Output
);

  wire [8:0] xor_1_out;

  assign xor_1_out = {9{1'b1}} ^ {1'b0, In};  // XOr xor_1, 9 bits wide
  Add #(.Bits(9)) add_1 (.a(xor_1_out), .b(9'h1), .c_i(1'b0), .s(Output));  // open: c_o
endmodule
