// Digital circuit 04.dig as structural Verilog
module _04 (
  input  [3:0] In,
  output [3:0] Output
);

  wire [2:0] demultiplexer_1_out_0, demultiplexer_1_out_1;
  wire [3:0] complement_1_output;

  Demultiplexer #(.Bits(3)) demultiplexer_1 (
    .sel(In[3]), .in(In[2:0]), .out_0(demultiplexer_1_out_0), .out_1(demultiplexer_1_out_1));
  complement complement_1 (.In(demultiplexer_1_out_1), .Output(complement_1_output));
  assign Output = {1'b0, demultiplexer_1_out_0} | complement_1_output;  // Or or_1, 4 bits wide
endmodule
