// Digital circuit complement.dig as structural Verilog
module complement (
  input  [2:0] In,
  output [3:0] Output
);

  wire [3:0] xor_1_out;

  assign xor_1_out = 4'b1111 ^ {1'b0, In};  // XOr xor_1, 4 bits wide
  Add #(.Bits(4)) add_1 (.a(xor_1_out), .b(4'b0001), .c_i(1'b0), .s(Output));  // open: c_o
endmodule
