// Digital circuit Template.dig as structural Verilog
module Template (
  input  [3:0] A,
  input  [3:0] B,
  input  [2:0] S,
  input  M,
  input  C,
  output [3:0] F
);

  wire [3:0] add_1_s, add_2_s, add_3_s, add_4_s, add_5_s, add_6_s, and_1_out, and_2_out, complement_1_out,
       complement_2_out, complement_3_out, complement_4_out, complement_5_out, multiplexer_1_out,
       multiplexer_2_out, multiplexer_3_out, nand_1_out, nor_1_out, not_1_out, or_1_out, xnor_1_out;

  complement complement_1 (.In(4'b0001), .Out(complement_1_out));
  complement complement_2 (.In(B), .Out(complement_2_out));
  complement complement_3 (.In(4'b0001), .Out(complement_3_out));
  complement complement_4 (.In(A), .Out(complement_4_out));
  complement complement_5 (.In(4'b0001), .Out(complement_5_out));
  Add #(.Bits(4)) add_1 (.a(A), .b(complement_1_out), .c_i(1'b0), .s(add_1_s));  // open: c_o
  Add #(.Bits(4)) add_2 (.a(A), .b(B), .c_i(1'b0), .s(add_2_s));  // open: c_o
  Add #(.Bits(4)) add_3 (.a(A), .b(complement_2_out), .c_i(1'b0), .s(add_3_s));  // open: c_o
  Add #(.Bits(4)) add_4 (.a(complement_4_out), .b(complement_5_out), .c_i(1'b0), .s(add_4_s));  // open: c_o
  Add #(.Bits(4)) add_5 (.a(add_3_s), .b(complement_3_out), .c_i(1'b0), .s(add_5_s));  // open: c_o
  assign not_1_out = ~A;  // Not not_1, 4 bits wide
  assign nand_1_out = ~(A & B);  // NAnd nand_1, 4 bits wide
  assign nor_1_out = ~(A | B);  // NOr nor_1, 4 bits wide
  assign xnor_1_out = ~(A ^ B);  // XNOr xnor_1, 4 bits wide
  assign and_1_out = A & B;  // And and_1, 4 bits wide
  assign or_1_out = A | B;  // Or or_1, 4 bits wide
  assign and_2_out = A & ~B;  // And and_2, 4 bits wide
  Multiplexer #(.Bits(4), .Selector_Bits(3)) multiplexer_1 (
    .sel(S), .in_0(A), .in_1(add_1_s), .in_2(add_2_s), .in_3(add_5_s), .in_4(add_4_s), .in_5(B),
    .in_6({A[2:0], 1'b0}), .in_7({1'b0, A[3:1]}), .out(multiplexer_1_out));
  Add #(.Bits(4)) add_6 (.a(multiplexer_1_out), .b(4'b0001), .c_i(1'b0), .s(add_6_s));  // open: c_o
  Multiplexer #(.Selector_Bits(3), .Bits(4)) multiplexer_2 (
    .sel(S), .in_0(not_1_out), .in_1(nand_1_out), .in_2(nor_1_out), .in_3(xnor_1_out), .in_4(and_1_out),
    .in_5(or_1_out), .in_6(and_2_out), .in_7(A), .out(multiplexer_2_out));
  Multiplexer #(.Bits(4)) multiplexer_3 (.sel(C), .in_0(multiplexer_1_out), .in_1(add_6_s), .out(multiplexer_3_out));
  Multiplexer #(.Bits(4)) multiplexer_4 (.sel(M), .in_0(multiplexer_2_out), .in_1(multiplexer_3_out), .out(F));
endmodule
