// Digital circuit complement.dig as structural Verilog
module complement (
  input  [3:0] In,
  output [3:0] Out
);

  wire [3:0] not_1_out;

  assign not_1_out = ~In;  // Not not_1, 4 bits wide
  Add #(.Bits(4)) add_1 (.a(not_1_out), .b(4'b0001), .c_i(1'b0), .s(Out));  // open: c_o
endmodule
