// Digital circuit Template - Copy.dig as structural Verilog
module Template___Copy (
  input  D,
  input  Clear,
  input  Clock,
  output Q,
  output Q_2
);

  wire nor_1_out, nor_2_out, nor_3_out, not_1_out, not_2_out, not_3_out;

  not not_1 (not_1_out, D);
  nor nor_1 (nor_1_out, not_1_out, Clear);
  not not_2 (not_2_out, Clock);
  not not_3 (not_3_out, nor_1_out);
  nor nor_2 (nor_2_out, not_2_out, nor_1_out);
  nor nor_3 (nor_3_out, not_3_out, not_2_out);
  nor nor_4 (Q_2, nor_3_out, Q);
  nor nor_5 (Q, Q_2, nor_2_out);
endmodule
