// Digital circuit Template.dig as structural Verilog
module Template (
  input  P,
  input  T,
  input  Clr,
  input  Load,
  input  Clock,
  input  D,
  input  C,
  input  B,
  input  A,
  output QD,
  output QC,
  output QB,
  output QA,
  output RCO
);

  wire and_1_out;
  wire [3:0] add_1_s, multiplexer_1_out;

  and and_1 (and_1_out, P, T, Clr, Load);
  Multiplexer #(.Bits(4), .Selector_Bits(2)) multiplexer_1 (
    .sel({Clr, Load}), .in_0({D, C, B, A}), .in_1(4'b0000), .in_2({D, C, B, A}), .in_3(add_1_s),
    .out(multiplexer_1_out));
  Add #(.Bits(4)) add_1 (.a({QD, QC, QB, QA}), .b(4'b0000), .c_i(and_1_out), .s(add_1_s));  // open: c_o
  D_FF #(.Bits(4)) d_ff_1 (.D(multiplexer_1_out), .C(Clock), .Q({QD, QC, QB, QA}));  // open: nQ
  and and_2 (RCO, QA, QB, QC, QD);
endmodule
