// Digital circuit 01.dig as structural Verilog
module _01 (
  input  P5,
  input  P10,
  input  P20,
  input  clock,
  input  Pcoffee,
  input  Ptea,
  input  Pchange,
  input  Pnext,
  input  reset,
  output CoffeeOut,
  output TeaOut,
  output [1:0] Change20,
  output [1:0] Change10,
  output [1:0] Change5,
  output [5:0] Balance
);

  wire add_1_c_o, and_1_out, and_2_out, and_3_out, and_4_out, and_5_out, BuyCoffee, BuyTea, comparator_1_eq,
       comparator_1_gt, comparator_2_eq, comparator_2_gt, comparator_3_eq, comparator_3_lt, d_ff_6_q,
       d_ff_7_q, d_ff_8_q, d_ff_9_q, d_ff_10_q, d_ff_11_q, d_ff_12_q, d_ff_13_nq, d_ff_14_nq, d_ff_15_nq,
       d_ff_16_nq, d_ff_17_nq, d_ff_18_nq, d_ff_19_nq, multiplexer_8_out, multiplexer_9_out,
       multiplexer_12_out, multiplexer_13_out, or_1_out, or_2_out, or_3_out, or_4_out, or_5_out, or_6_out,
       or_7_out, P5_t, P10_t, P20_t, Pchange_t, Pcoffee_t, Pnext_t, Ptea_t;
  wire [1:0] div_1_q, multiplexer_1_out, multiplexer_2_out, multiplexer_7_out, multiplexer_10_out,
       multiplexer_15_out, multiplexer_16_out;
  wire [5:0] add_1_s, div_1_r, div_2_q, div_2_r, div_3_q, div_3_r, multiplexer_3_out, multiplexer_4_out,
       multiplexer_5_out, multiplexer_6_out, multiplexer_11_out, multiplexer_14_out, sub_1_s, sub_2_s;
  wire [5:2] div_1_q_2;

  Multiplexer #(.Bits(2)) multiplexer_1 (.sel(reset), .in_0(multiplexer_2_out), .in_1(2'b00), .out(multiplexer_1_out));
  Div #(.Bits(6)) div_1 (.a(Balance), .b(6'b010100), .q({div_1_q_2, div_1_q}), .r(div_1_r));
  Multiplexer #(.Bits(2)) multiplexer_2 (.sel(Pchange_t), .in_0(Change20), .in_1(div_1_q), .out(multiplexer_2_out));
  D_FF #(.Bits(2)) d_ff_1 (.D(multiplexer_1_out), .C(clock), .Q(Change20));  // open: nQ
  Comparator #(.Bits(6)) comparator_1 (
    .a(Balance), .b(6'b010100), .gt(comparator_1_gt), .eq(comparator_1_eq));  // open: lt
  or or_1 (or_1_out, CoffeeOut, TeaOut);
  Comparator #(.Bits(6)) comparator_2 (
    .a(Balance), .b(6'b011001), .gt(comparator_2_gt), .eq(comparator_2_eq));  // open: lt
  or or_2 (or_2_out, CoffeeOut, TeaOut);
  Multiplexer #(.Selector_Bits(3), .Bits(6)) multiplexer_3 (
    .sel({P20_t, P10_t, P5_t}), .in_0({6{1'b0}}), .in_1(6'b000101), .in_2(6'b001010), .in_3({6{1'b0}}),
    .in_4(6'b010100), .in_5({6{1'b0}}), .in_6({6{1'b0}}), .in_7({6{1'b0}}), .out(multiplexer_3_out));
  and and_1 (and_1_out, Pnext_t, or_2_out);
  Sub #(.Bits(6)) sub_1 (.a(multiplexer_4_out), .b(6'b011001), .c_i(1'b0), .s(sub_1_s));  // open: c_o
  Sub #(.Bits(6)) sub_2 (.a(multiplexer_5_out), .b(6'b010100), .c_i(1'b0), .s(sub_2_s));  // open: c_o
  or or_3 (or_3_out, comparator_1_gt, comparator_1_eq);
  and and_2 (and_2_out, Pnext_t, or_1_out);
  or or_4 (or_4_out, comparator_2_gt, comparator_2_eq);
  Multiplexer #(.Bits(6)) multiplexer_4 (
    .sel(and_5_out), .in_0(multiplexer_11_out), .in_1(add_1_s), .out(multiplexer_4_out));
  Multiplexer #(.Bits(6)) multiplexer_5 (
    .sel(BuyCoffee), .in_0(multiplexer_4_out), .in_1(sub_1_s), .out(multiplexer_5_out));
  Multiplexer #(.Bits(6)) multiplexer_6 (
    .sel(BuyTea), .in_0(multiplexer_5_out), .in_1(sub_2_s), .out(multiplexer_6_out));
  and and_3 (and_3_out, Ptea_t, ~TeaOut, ~CoffeeOut, or_3_out);  // And
  or or_5 (or_5_out, reset, Pchange_t, and_2_out);
  and and_4 (and_4_out, Pcoffee_t, ~TeaOut, ~CoffeeOut, or_4_out);  // And
  or or_6 (or_6_out, reset, Pchange_t, and_1_out);
  Add #(.Bits(6)) add_1 (.a(multiplexer_11_out), .b(multiplexer_3_out), .c_i(1'b0), .s(add_1_s), .c_o(add_1_c_o));
  Multiplexer #(.Bits(2)) multiplexer_7 (.sel(reset), .in_0(multiplexer_10_out), .in_1(2'b00), .out(multiplexer_7_out));
  Div #(.Bits(6)) div_2 (.a(div_1_r), .b(6'b001010), .q(div_2_q), .r(div_2_r));
  Multiplexer multiplexer_8 (.sel(or_5_out), .in_0(multiplexer_12_out), .in_1(1'b0), .out(multiplexer_8_out));
  Multiplexer multiplexer_9 (.sel(or_6_out), .in_0(multiplexer_13_out), .in_1(1'b0), .out(multiplexer_9_out));
  Comparator #(.Bits(6)) comparator_3 (
    .a(add_1_s), .b(6'b110010), .eq(comparator_3_eq), .lt(comparator_3_lt));  // open: gt
  Multiplexer #(.Bits(2)) multiplexer_10 (
    .sel(Pchange_t), .in_0(Change10), .in_1(div_2_q[1:0]), .out(multiplexer_10_out));
  D_FF #(.Bits(2)) d_ff_2 (.D(multiplexer_7_out), .C(clock), .Q(Change10));  // open: nQ
  Multiplexer #(.Bits(6)) multiplexer_11 (.sel(reset), .in_0(Balance), .in_1({6{1'b0}}), .out(multiplexer_11_out));
  or or_7 (or_7_out, comparator_3_eq, comparator_3_lt);
  and and_5 (and_5_out, ~TeaOut, ~CoffeeOut, ~add_1_c_o, or_7_out);  // And
  Multiplexer multiplexer_12 (.sel(and_3_out), .in_0(TeaOut), .in_1(1'b1), .out(multiplexer_12_out));
  D_FF d_ff_3 (.D(multiplexer_8_out), .C(clock), .Q(TeaOut));  // open: nQ
  Multiplexer multiplexer_13 (.sel(and_4_out), .in_0(CoffeeOut), .in_1(1'b1), .out(multiplexer_13_out));
  D_FF d_ff_4 (.D(multiplexer_9_out), .C(clock), .Q(CoffeeOut));  // open: nQ
  D_FF #(.Bits(6)) u_Balance (.D(multiplexer_14_out), .C(clock), .Q(Balance));  // open: nQ
  Multiplexer #(.Bits(6)) multiplexer_14 (
    .sel(Pchange_t), .in_0(multiplexer_6_out), .in_1(div_3_r), .out(multiplexer_14_out));
  and and_6 (BuyTea, ~TeaOut, multiplexer_8_out);  // And
  and and_7 (BuyCoffee, ~CoffeeOut, multiplexer_9_out);  // And
  Multiplexer #(.Bits(2)) multiplexer_15 (
    .sel(reset), .in_0(multiplexer_16_out), .in_1(2'b00), .out(multiplexer_15_out));
  Div #(.Bits(6)) div_3 (.a(div_2_r), .b(6'b000101), .q(div_3_q), .r(div_3_r));
  Multiplexer #(.Bits(2)) multiplexer_16 (
    .sel(Pchange_t), .in_0(Change5), .in_1(div_3_q[1:0]), .out(multiplexer_16_out));
  D_FF #(.Bits(2)) d_ff_5 (.D(multiplexer_15_out), .C(clock), .Q(Change5));  // open: nQ
  D_FF d_ff_6 (.D(Pcoffee), .C(clock), .Q(d_ff_6_q));  // open: nQ
  D_FF d_ff_7 (.D(Ptea), .C(clock), .Q(d_ff_7_q));  // open: nQ
  D_FF d_ff_8 (.D(Pchange), .C(clock), .Q(d_ff_8_q));  // open: nQ
  D_FF d_ff_9 (.D(Pnext), .C(clock), .Q(d_ff_9_q));  // open: nQ
  D_FF d_ff_10 (.D(P5), .C(clock), .Q(d_ff_10_q));  // open: nQ
  D_FF d_ff_11 (.D(P10), .C(clock), .Q(d_ff_11_q));  // open: nQ
  D_FF d_ff_12 (.D(P20), .C(clock), .Q(d_ff_12_q));  // open: nQ
  D_FF d_ff_13 (.D(d_ff_6_q), .C(clock), .nQ(d_ff_13_nq));  // open: Q
  D_FF d_ff_14 (.D(d_ff_7_q), .C(clock), .nQ(d_ff_14_nq));  // open: Q
  D_FF d_ff_15 (.D(d_ff_8_q), .C(clock), .nQ(d_ff_15_nq));  // open: Q
  D_FF d_ff_16 (.D(d_ff_9_q), .C(clock), .nQ(d_ff_16_nq));  // open: Q
  D_FF d_ff_17 (.D(d_ff_10_q), .C(clock), .nQ(d_ff_17_nq));  // open: Q
  D_FF d_ff_18 (.D(d_ff_11_q), .C(clock), .nQ(d_ff_18_nq));  // open: Q
  D_FF d_ff_19 (.D(d_ff_12_q), .C(clock), .nQ(d_ff_19_nq));  // open: Q
  and and_8 (Pcoffee_t, d_ff_6_q, d_ff_13_nq);
  and and_9 (Ptea_t, d_ff_7_q, d_ff_14_nq);
  and and_10 (Pchange_t, d_ff_8_q, d_ff_15_nq);
  and and_11 (Pnext_t, d_ff_9_q, d_ff_16_nq);
  and and_12 (P5_t, d_ff_10_q, d_ff_17_nq);
  and and_13 (P10_t, d_ff_11_q, d_ff_18_nq);
  and and_14 (P20_t, d_ff_12_q, d_ff_19_nq);

  // Other names for the same wires on the sheet: Clk = clock
endmodule
