// Digital circuit test2.dig as structural Verilog
module test2 (
  input  clock,
  input  P5,
  input  P10,
  input  P20,
  input  reset,
  input  Pchange,
  input  Pnext,
  input  Ptea,
  input  Pcoffee,
  output [5:0] Balance,
  output CoffeeOut,
  output TeaOut,
  output [1:0] Change5,
  output [1:0] Change10,
  output [1:0] Change20
);

  wire and_1_out, and_2_out, and_7_out, and_8_out, and_9_out, comparator_1_gt, comparator_2_gt,
       comparator_3_lt, comparator_4_lt, comparator_5_lt, d_ff_3_q, d_ff_4_q, d_ff_5_nq, d_ff_6_nq,
       d_ff_7_nq, d_ff_8_nq, d_ff_9_q, d_ff_10_q, d_ff_11_q, d_ff_12_q, d_ff_13_q, d_ff_14_q, d_ff_15_q,
       d_ff_16_q, d_ff_20_nq, d_ff_21_nq, d_ff_22_nq, d_ff_24_q, d_ff_25_q, d_ff_26_q, d_ff_27_q, d_ff_28_q,
       d_ff_29_q, or_1_out, P5_t, P10_t, P20_t, PChange_Reset, Pchange_t, Pcoffee_t, Pnext_t, Ptea_t,
       rs_ff_as_1_q, rs_ff_as_2_q;
  wire [5:0] add_1_s, Calculate_out, d_ff_17_q, div_1_q, div_1_r, div_2_q, div_2_r, div_3_q,
       multiplexer_2_out, multiplexer_3_out, multiplexer_4_out;
  wire [5:2] d_ff_18_q, d_ff_19_q, d_ff_23_q;

  or or_1 (or_1_out, Pchange_t, Pnext_t, reset);
  or or_2 (PChange_Reset, Pchange_t, reset);
  RS_FF_AS rs_ff_as_1 (.S(Pcoffee_t), .R(or_1_out), .Q(rs_ff_as_1_q));  // open: nQ
  RS_FF_AS rs_ff_as_2 (.S(Ptea_t), .R(or_1_out), .Q(rs_ff_as_2_q));  // open: nQ
  Comparator #(.Bits(6)) comparator_1 (.a(Balance), .b(6'b011000), .gt(comparator_1_gt));  // open: eq, lt
  Comparator #(.Bits(6)) comparator_2 (.a(Balance), .b(6'b010011), .gt(comparator_2_gt));  // open: eq, lt
  D_FF d_ff_1 (.D(rs_ff_as_1_q), .C(clock), .Q(CoffeeOut));  // open: nQ
  D_FF d_ff_2 (.D(rs_ff_as_2_q), .C(clock), .Q(TeaOut));  // open: nQ
  and and_1 (and_1_out, ~CoffeeOut, ~TeaOut, comparator_1_gt, Pcoffee);  // And
  and and_2 (and_2_out, ~CoffeeOut, ~TeaOut, comparator_2_gt, Ptea);  // And
  D_FF d_ff_3 (.D(Pchange), .C(clock), .Q(d_ff_3_q));  // open: nQ
  D_FF d_ff_4 (.D(Pnext), .C(clock), .Q(d_ff_4_q));  // open: nQ
  D_FF d_ff_5 (.D(and_1_out), .C(clock), .nQ(d_ff_5_nq));  // open: Q
  D_FF d_ff_6 (.D(and_2_out), .C(clock), .nQ(d_ff_6_nq));  // open: Q
  D_FF d_ff_7 (.D(d_ff_3_q), .C(clock), .nQ(d_ff_7_nq));  // open: Q
  D_FF d_ff_8 (.D(d_ff_4_q), .C(clock), .nQ(d_ff_8_nq));  // open: Q
  D_FF d_ff_9 (.D(and_1_out), .C(clock), .Q(d_ff_9_q));  // open: nQ
  D_FF d_ff_10 (.D(d_ff_5_nq), .C(clock), .Q(d_ff_10_q));  // open: nQ
  D_FF d_ff_11 (.D(and_2_out), .C(clock), .Q(d_ff_11_q));  // open: nQ
  D_FF d_ff_12 (.D(d_ff_6_nq), .C(clock), .Q(d_ff_12_q));  // open: nQ
  D_FF d_ff_13 (.D(d_ff_3_q), .C(clock), .Q(d_ff_13_q));  // open: nQ
  D_FF d_ff_14 (.D(d_ff_7_nq), .C(clock), .Q(d_ff_14_q));  // open: nQ
  D_FF d_ff_15 (.D(d_ff_4_q), .C(clock), .Q(d_ff_15_q));  // open: nQ
  D_FF d_ff_16 (.D(d_ff_8_nq), .C(clock), .Q(d_ff_16_q));  // open: nQ
  and and_3 (Pcoffee_t, d_ff_9_q, d_ff_10_q);
  and and_4 (Ptea_t, d_ff_11_q, d_ff_12_q);
  and and_5 (Pchange_t, d_ff_13_q, d_ff_14_q);
  and and_6 (Pnext_t, d_ff_15_q, d_ff_16_q);
  LookUpTable #(.Bits(6)) Calculate (
    .in0(P5_t), .in1(P10_t), .in2(P20_t), .in3(Pcoffee_t), .in4(Ptea_t), .out(Calculate_out));
  Add #(.Bits(6)) add_1 (.a(Balance), .b(Calculate_out), .c_i(1'b0), .s(add_1_s));  // open: c_o
  D_FF #(.Bits(6)) d_ff_17 (.D(add_1_s), .C(clock), .Q(d_ff_17_q));  // open: nQ
  Multiplexer #(.Bits(6)) multiplexer_1 (.sel(PChange_Reset), .in_0(d_ff_17_q), .in_1({6{1'b0}}), .out(Balance));
  Div #(.Bits(6)) div_1 (.a(d_ff_17_q), .b(6'b010100), .q(div_1_q), .r(div_1_r));
  Div #(.Bits(6)) div_2 (.a(div_1_r), .b(6'b001010), .q(div_2_q), .r(div_2_r));
  Div #(.Bits(6)) div_3 (.a(div_2_r), .b(6'b000101), .q(div_3_q));  // open: r
  Comparator #(.Bits(6)) comparator_3 (.a(Balance), .b(6'b101110), .lt(comparator_3_lt));  // open: gt, eq
  Comparator #(.Bits(6)) comparator_4 (.a(Balance), .b(6'b101001), .lt(comparator_4_lt));  // open: gt, eq
  Comparator #(.Bits(6)) comparator_5 (.a(Balance), .b(6'b011111), .lt(comparator_5_lt));  // open: gt, eq
  and and_7 (and_7_out, ~CoffeeOut, ~TeaOut, comparator_3_lt, P5);  // And
  and and_8 (and_8_out, ~CoffeeOut, ~TeaOut, comparator_4_lt, P10);  // And
  and and_9 (and_9_out, ~CoffeeOut, ~TeaOut, comparator_5_lt, P20);  // And
  Multiplexer #(.Bits(6)) multiplexer_2 (.sel(reset), .in_0(div_2_q), .in_1({6{1'b0}}), .out(multiplexer_2_out));
  Multiplexer #(.Bits(6)) multiplexer_3 (.sel(reset), .in_0(div_3_q), .in_1({6{1'b0}}), .out(multiplexer_3_out));
  Multiplexer #(.Bits(6)) multiplexer_4 (.sel(reset), .in_0(div_1_q), .in_1({6{1'b0}}), .out(multiplexer_4_out));
  D_FF #(.Bits(6)) d_ff_18 (.D(multiplexer_2_out), .C(PChange_Reset), .Q({d_ff_18_q, Change10}));  // open: nQ
  D_FF #(.Bits(6)) d_ff_19 (.D(multiplexer_3_out), .C(PChange_Reset), .Q({d_ff_19_q, Change5}));  // open: nQ
  D_FF d_ff_20 (.D(and_7_out), .C(clock), .nQ(d_ff_20_nq));  // open: Q
  D_FF d_ff_21 (.D(and_8_out), .C(clock), .nQ(d_ff_21_nq));  // open: Q
  D_FF d_ff_22 (.D(and_9_out), .C(clock), .nQ(d_ff_22_nq));  // open: Q
  D_FF #(.Bits(6)) d_ff_23 (.D(multiplexer_4_out), .C(PChange_Reset), .Q({d_ff_23_q, Change20}));  // open: nQ
  D_FF d_ff_24 (.D(and_7_out), .C(clock), .Q(d_ff_24_q));  // open: nQ
  D_FF d_ff_25 (.D(d_ff_20_nq), .C(clock), .Q(d_ff_25_q));  // open: nQ
  D_FF d_ff_26 (.D(and_8_out), .C(clock), .Q(d_ff_26_q));  // open: nQ
  D_FF d_ff_27 (.D(d_ff_21_nq), .C(clock), .Q(d_ff_27_q));  // open: nQ
  D_FF d_ff_28 (.D(and_9_out), .C(clock), .Q(d_ff_28_q));  // open: nQ
  D_FF d_ff_29 (.D(d_ff_22_nq), .C(clock), .Q(d_ff_29_q));  // open: nQ
  and and_10 (P5_t, d_ff_24_q, d_ff_25_q);
  and and_11 (P10_t, d_ff_26_q, d_ff_27_q);
  and and_12 (P20_t, d_ff_28_q, d_ff_29_q);

  // Notes on the sheet:
  //   contents of Calculate (hex, n*v repeats v):
  //   0,5,a,0,14,0,0,0,ffffffffffffffe7,7*0,ffffffffffffffec
endmodule
