// Digital circuit 01.dig as structural Verilog
module _01 (
  input  [7:0] Input,
  input  Add,
  input  Reset,
  input  clk,
  output [11:0] Output
);

  wire [11:0] add_1_s, multiplexer_1_out;

  Add #(.Bits(12)) add_1 (.a(Output), .b({4'b0000, Input}), .c_i(1'b0), .s(add_1_s));  // open: c_o
  Multiplexer #(.Bits(12)) multiplexer_1 (.sel(Add), .in_0(Output), .in_1(add_1_s), .out(multiplexer_1_out));
  D_FF_AS #(.Bits(12)) d_ff_as_1 (.Set(1'b0), .D(multiplexer_1_out), .C(clk), .Clr(Reset), .Q(Output));  // open: nQ
endmodule
