// Digital circuit 01_20.dig as structural Verilog
module _01_20 (
  input  [7:0] A,
  input  [7:0] B,
  input  start,
  input  clk,
  output Busy,
  output [7:0] GCD
);

  wire a__gt__b, a__lt__b, and_1_out, comparator_1_eq, d_ff_1_q, d_ff_2_nq, finish, start_t;
  wire [3:0] div_1_q, div_1_r;
  wire [7:0] a_t, b_t, multiplexer_1_out, multiplexer_2_out, multiplexer_3_out, multiplexer_4_out,
       multiplexer_5_out, sub_1_s, sub_2_s;
  wire [7:4] div_1_q_2, div_1_r_2;

  D_FF d_ff_1 (.D(start), .C(clk), .Q(d_ff_1_q));  // open: nQ
  D_FF d_ff_2 (.D(d_ff_1_q), .C(clk), .nQ(d_ff_2_nq));  // open: Q
  and and_1 (and_1_out, d_ff_1_q, d_ff_2_nq);
  JK_FF jk_ff_1 (.J(and_1_out), .C(clk), .K(finish), .Q(start_t));  // open: nQ
  Multiplexer #(.Bits(8)) multiplexer_1 (.sel(start_t), .in_0(B), .in_1(multiplexer_4_out), .out(multiplexer_1_out));
  Multiplexer #(.Bits(8)) multiplexer_2 (.sel(start_t), .in_0(A), .in_1(multiplexer_3_out), .out(multiplexer_2_out));
  Multiplexer #(.Bits(8)) multiplexer_3 (.sel(a__gt__b), .in_0(a_t), .in_1(sub_1_s), .out(multiplexer_3_out));
  Multiplexer #(.Bits(8)) multiplexer_4 (.sel(a__lt__b), .in_0(b_t), .in_1(sub_2_s), .out(multiplexer_4_out));
  D_FF #(.Bits(8)) u_A (.D(multiplexer_2_out), .C(clk), .Q(a_t));  // open: nQ
  D_FF #(.Bits(8)) d_ff_3 (.D(multiplexer_1_out), .C(clk), .Q(b_t));  // open: nQ
  Sub #(.Bits(8)) sub_1 (.a(a_t), .b(b_t), .c_i(1'b0), .s(sub_1_s));  // open: c_o
  Sub #(.Bits(8)) sub_2 (.a(b_t), .b(a_t), .c_i(1'b0), .s(sub_2_s));  // open: c_o
  Comparator #(.Bits(8)) comparator_1 (.a(a_t), .b(b_t), .gt(a__gt__b), .eq(comparator_1_eq), .lt(a__lt__b));
  Multiplexer #(.Bits(8)) multiplexer_5 (.sel(finish), .in_0(GCD), .in_1(a_t), .out(multiplexer_5_out));
  and and_2 (finish, comparator_1_eq, start_t);
  D_FF #(.Bits(8)) d_ff_4 (.D(multiplexer_5_out), .C(clk), .Q(GCD));  // open: nQ
  Seven_Seg_Hex seven_seg_hex_1 (.d(div_1_q), .dp(1'b0));
  Div #(.Bits(8)) div_1 (.a(GCD), .b(8'ha), .q({div_1_q_2, div_1_q}), .r({div_1_r_2, div_1_r}));
  and and_3 (Busy, start_t, ~finish);  // And
  Seven_Seg_Hex seven_seg_hex_2 (.d(div_1_r), .dp(1'b0));
endmodule
