// Digital circuit 02.dig as structural Verilog
module _02 (
  input  Push,
  input  clk
);

  wire add_1_c_o, and_1_out, and_2_out, d_ff_1_q, d_ff_2_nq;
  wire [3:0] add_1_s, d_ff_as_1_q, multiplexer_1_out, multiplexer_2_out;

  D_FF d_ff_1 (.D(Push), .C(clk), .Q(d_ff_1_q));  // open: nQ
  D_FF d_ff_2 (.D(d_ff_1_q), .C(clk), .nQ(d_ff_2_nq));  // open: Q
  and and_1 (and_1_out, d_ff_1_q, d_ff_2_nq);
  Multiplexer #(.Bits(4)) multiplexer_1 (
    .sel(and_2_out), .in_0(multiplexer_2_out), .in_1(4'b0011), .out(multiplexer_1_out));
  Multiplexer #(.Bits(4)) multiplexer_2 (.sel(and_1_out), .in_0(d_ff_as_1_q), .in_1(add_1_s), .out(multiplexer_2_out));
  and and_2 (and_2_out, add_1_c_o, and_1_out);
  D_FF_AS #(.Bits(4), .Default(3)) d_ff_as_1 (
    .Set(1'b0), .D(multiplexer_1_out), .C(clk), .Clr(1'b0), .Q(d_ff_as_1_q));  // open: nQ
  Add #(.Bits(4)) add_1 (.a(d_ff_as_1_q), .b(4'b0011), .c_i(1'b0), .s(add_1_s), .c_o(add_1_c_o));
  LED led_1 (.in(add_1_c_o));
  Seven_Seg_Hex seven_seg_hex_1 (.d(d_ff_as_1_q), .dp(1'b0));
endmodule
