// Digital circuit 02_final.dig as structural Verilog
module _02_final (
  input  [15:0] A,
  input  \input ,
  input  clk,
  output [7:0] sqrt,
  output busy
);

  wire and_1_out, and_2_out, and_3_out, and_4_out, comparator_1_eq, comparator_3_eq, comparator_5_eq,
       comparator_7_eq, comparator_9_lt, comparator_10_eq, comparator_11_eq, counterpreset_1_ovf,
       counterpreset_2_ovf, counterpreset_3_ovf, d1, d2, d3, d4, f0, f1, f2, f3, f4, finish, input_t,
       not_1_out, not_2_out, not_3_out, not_4_out, or_5_out, or_6_out;
  wire [7:0] c1, c2, c3, c4, multiplexer_1_out, multiplexer_2_out, multiplexer_3_out, multiplexer_4_out,
       multiplexer_5_out, multiplexer_6_out, sub_1_s, sub_2_s, sub_3_s, sub_4_s, sub_5_s;
  wire [15:0] div_1_q, div_2_q, div_3_q, div_4_q, div_5_q;

  JK_FF jk_ff_1 (.J(\input ), .C(clk), .K(finish), .Q(input_t));  // open: nQ
  and and_1 (and_1_out, input_t, ~counterpreset_1_ovf, ~finish);  // And
  and and_2 (and_2_out, input_t, ~counterpreset_2_ovf, ~finish);  // And
  and and_3 (and_3_out, input_t, ~counterpreset_3_ovf, ~finish);  // And
  and and_4 (and_4_out, input_t, ~finish);  // And
  not not_1 (not_1_out, input_t);
  not not_2 (not_2_out, input_t);
  not not_3 (not_3_out, input_t);
  CounterPreset #(.Bits(8)) counterpreset_1 (
    .en(and_1_out), .C(clk), .dir(1'b0), .in(8'h2), .ld(not_4_out), .clr(finish), .out(c1),
    .ovf(counterpreset_1_ovf));
  not not_4 (not_4_out, input_t);
  CounterPreset #(.Bits(8)) counterpreset_2 (
    .en(and_2_out), .C(clk), .dir(1'b0), .in(8'h41), .ld(not_1_out), .clr(finish), .out(c2),
    .ovf(counterpreset_2_ovf));
  CounterPreset #(.Bits(8)) counterpreset_3 (
    .en(and_3_out), .C(clk), .dir(1'b0), .in(8'h81), .ld(not_2_out), .clr(finish), .out(c3),
    .ovf(counterpreset_3_ovf));
  CounterPreset #(.Bits(8)) counterpreset_4 (
    .en(and_4_out), .C(clk), .dir(1'b0), .in(8'hc1), .ld(not_3_out), .clr(finish), .out(c4));  // open: ovf
  Div #(.Bits(16)) div_1 (.a(A), .b({{8{1'b0}}, c2}), .q(div_1_q));  // open: r
  Div #(.Bits(16)) div_2 (.a(A), .b({{8{1'b0}}, c3}), .q(div_2_q));  // open: r
  Div #(.Bits(16)) div_3 (.a(A), .b({{8{1'b0}}, c4}), .q(div_3_q));  // open: r
  Div #(.Bits(16)) div_4 (.a(A), .b({{8{1'b0}}, c1}), .q(div_4_q));  // open: r
  Sub #(.Bits(8)) sub_1 (.a(c1), .b({8{1'b0}}), .c_i(1'b1), .s(sub_1_s));  // open: c_o
  Sub #(.Bits(8)) sub_2 (.a(c2), .b({8{1'b0}}), .c_i(1'b1), .s(sub_2_s));  // open: c_o
  Sub #(.Bits(8)) sub_3 (.a(c3), .b({8{1'b0}}), .c_i(1'b1), .s(sub_3_s));  // open: c_o
  Sub #(.Bits(8)) sub_4 (.a(c4), .b({8{1'b0}}), .c_i(1'b1), .s(sub_4_s));  // open: c_o
  Comparator #(.Bits(8)) comparator_1 (.a(div_1_q[7:0]), .b(c2), .eq(comparator_1_eq));  // open: gt, lt
  Comparator #(.Bits(8)) comparator_2 (.a(div_1_q[7:0]), .b(sub_2_s), .eq(d2));  // open: gt, lt
  Comparator #(.Bits(8)) comparator_3 (.a(div_2_q[7:0]), .b(c3), .eq(comparator_3_eq));  // open: gt, lt
  Comparator #(.Bits(8)) comparator_4 (.a(div_2_q[7:0]), .b(sub_3_s), .eq(d3));  // open: gt, lt
  Comparator #(.Bits(8)) comparator_5 (.a(div_3_q[7:0]), .b(c4), .eq(comparator_5_eq));  // open: gt, lt
  Comparator #(.Bits(8)) comparator_6 (.a(div_3_q[7:0]), .b(sub_4_s), .eq(d4));  // open: gt, lt
  Comparator #(.Bits(8)) comparator_7 (.a(div_4_q[7:0]), .b(c1), .eq(comparator_7_eq));  // open: gt, lt
  Comparator #(.Bits(8)) comparator_8 (.a(div_4_q[7:0]), .b(sub_1_s), .eq(d1));  // open: gt, lt
  or or_1 (f3, comparator_3_eq, d3);
  or or_2 (f4, comparator_5_eq, d4);
  or or_3 (f1, comparator_7_eq, d1);
  or or_4 (f2, comparator_1_eq, d2);
  Multiplexer #(.Selector_Bits(4), .Bits(8)) multiplexer_1 (
    .sel({f4, f3, f2, f1}), .in_0({8{1'b0}}), .in_1(c1), .in_2(c2), .in_3({8{1'b0}}), .in_4(c3),
    .in_5({8{1'b0}}), .in_6({8{1'b0}}), .in_7({8{1'b0}}), .in_8(c4), .in_9({8{1'b0}}), .in_10({8{1'b0}}),
    .in_11({8{1'b0}}), .in_12({8{1'b0}}), .in_13({8{1'b0}}), .in_14({8{1'b0}}), .in_15({8{1'b0}}),
    .out(multiplexer_1_out));
  Sub #(.Bits(8)) sub_5 (.a(multiplexer_1_out), .b({8{1'b0}}), .c_i(1'b1), .s(sub_5_s));  // open: c_o
  or or_5 (or_5_out, d1, d2, d3, d4);
  and and_5 (busy, input_t, ~finish);  // And
  Div #(.Bits(16)) div_5 (.a(A), .b(16'h100), .q(div_5_q));  // open: r
  Multiplexer #(.Bits(8)) multiplexer_2 (
    .sel(or_5_out), .in_0(multiplexer_1_out), .in_1(sub_5_s), .out(multiplexer_2_out));
  Comparator #(.Bits(16)) comparator_9 (.a(A), .b(16'h4), .lt(comparator_9_lt));  // open: gt, eq
  Multiplexer #(.Bits(8)) multiplexer_3 (
    .sel(comparator_9_lt), .in_0(multiplexer_4_out), .in_1(8'h1), .out(multiplexer_3_out));
  or or_6 (or_6_out, f0, f1, f2, f3, f4);
  Comparator #(.Bits(16)) comparator_10 (.a(div_5_q), .b(16'hff), .eq(comparator_10_eq));  // open: gt, lt
  Multiplexer #(.Bits(8)) multiplexer_4 (
    .sel(comparator_10_eq), .in_0(multiplexer_2_out), .in_1({8{1'b1}}), .out(multiplexer_4_out));
  Comparator #(.Bits(16)) comparator_11 (.a(A), .b({16{1'b0}}), .eq(comparator_11_eq));  // open: gt, lt
  and and_6 (finish, input_t, or_6_out);
  Multiplexer #(.Bits(8)) multiplexer_5 (
    .sel(comparator_11_eq), .in_0(multiplexer_3_out), .in_1({8{1'b0}}), .out(multiplexer_5_out));
  or or_7 (f0, comparator_11_eq, comparator_10_eq, comparator_9_lt);
  Multiplexer #(.Bits(8)) multiplexer_6 (.sel(finish), .in_0(sqrt), .in_1(multiplexer_5_out), .out(multiplexer_6_out));
  D_FF #(.Bits(8)) d_ff_1 (.D(multiplexer_6_out), .C(clk), .Q(sqrt));  // open: nQ

  // Notes on the sheet:
  //   clk: Hz: 200
endmodule

/* Test case TestCase1:
clk A input sqrt busy
0 0 0 0 0
1 0 0 0 0
0 0 0 0 0
1 0 0 0 0
0 0 1 X X
1 0 1 X X
repeat (80) C 0 0 X X
0 0 0 0 0
1 0 0 0 0
*/

/* Test case TestCase2:
clk A input sqrt busy
0 0 0 0 0
1 0 0 0 0
0 0 0 0 0
1 0 0 0 0
0 1 1 X X
1 1 1 X X
repeat (80) C 1 0 X X
0 0 0 1 0
1 0 0 1 0
*/

/* Test case TestCase3:
clk A input sqrt busy
0 0 0 0 0
1 0 0 0 0
0 0 0 0 0
1 0 0 0 0
0 4 1 X X
1 4 1 X X
repeat (80) C 4 0 X X
0 0 0 2 0
1 0 0 2 0
*/

/* Test case TestCase4:
clk A input sqrt busy
0 0 0 0 0
1 0 0 0 0
0 0 0 0 0
1 0 0 0 0
0 9 1 X X
1 9 1 X X
repeat (80) C 9 0 X X
0 0 0 3 0
1 0 0 3 0
*/

/* Test case TestCase5:
clk A input sqrt busy
0 0 0 0 0
1 0 0 0 0
0 0 0 0 0
1 0 0 0 0
0 8 1 X X
1 8 1 X X
repeat (80) C 8 0 X X
0 0 0 2 0
1 0 0 2 0
*/
