// Digital circuit 2021_final_1.dig as structural Verilog
module _2021_final_1 (
  input  Add,
  input  [7:0] Number,
  input  Reset,
  input  clk,
  output [11:0] out_5
);

  wire AddSig, d_ff_as_1_q;
  wire [3:0] div_1_q, div_2_q, div_3_r;
  wire [11:0] add_1_s, div_1_r, multiplexer_1_out;
  wire [11:4] div_1_q_2, div_2_q_2, div_3_r_2;

  D_FF_AS d_ff_as_1 (.Set(1'b0), .D(1'b1), .C(Add), .Clr(AddSig), .Q(d_ff_as_1_q));  // open: nQ
  Multiplexer #(.Bits(12)) multiplexer_1 (
    .sel(AddSig), .in_0({12{1'b0}}), .in_1({4'b0000, Number}), .out(multiplexer_1_out));
  D_FF_AS d_ff_as_2 (.Set(1'b0), .D(d_ff_as_1_q), .C(clk), .Clr(1'b0), .Q(AddSig));  // open: nQ
  Add #(.Bits(12)) add_1 (.a(multiplexer_1_out), .b(out_5), .c_i(1'b0), .s(add_1_s));  // open: c_o
  D_FF_AS #(.Bits(12)) d_ff_as_3 (.Set(1'b0), .D(add_1_s), .C(clk), .Clr(Reset), .Q(out_5));  // open: nQ
  Seven_Seg_Hex seven_seg_hex_1 (.d(div_1_q), .dp(1'b0));
  Div #(.Bits(12)) div_1 (.a(out_5), .b(12'h64), .q({div_1_q_2, div_1_q}), .r(div_1_r));
  Seven_Seg_Hex seven_seg_hex_2 (.d(div_2_q), .dp(1'b0));
  Div #(.Bits(12)) div_2 (.a(div_1_r), .b(12'ha), .q({div_2_q_2, div_2_q}));  // open: r
  Seven_Seg_Hex seven_seg_hex_3 (.d(div_3_r), .dp(1'b0));
  Div #(.Bits(12)) div_3 (.a(out_5), .b(12'ha), .r({div_3_r_2, div_3_r}));  // open: q

  // Other names for the same wires on the sheet: CurrentSum[11:0] = out_5
endmodule
